# Fritzing sketch extended-smart-doorbell (saved by Fritzing 0.9.10b)
breadboards: 1

parts:
  Q1 = NPN-Transistor [package="TO92 [THT]"]
  WeMos_D1_Mini1 = WeMos D1 Mini  # not connected
  D3 = Rectifier Diode [part_number=1N4001 package="Melf DO-213 AB [SMD]"]

nets:
  N1: Q1.B, D3.anode

notes:
  5V Power Supply
  Gong
