# Fritzing sketch smart-doorbell-wiring (saved by Fritzing 0.9.10b)
breadboards: 1

parts:
  SHELLY1 = SHELLY1
  S1 = Pushbutton [package="[THT]"]
  J1 = Piezo Speaker

nets:
  N1: SHELLY1.connector3, J1.pin2
  N2: SHELLY1.connector5, S1.Pin_1, S1.Pin_2
  N3: SHELLY1.connector6, S1.Pin_3, S1.Pin_4

notes:
  12VDC
  Gong
  8VAC

custom parts:
  SHELLY1: DOMOTICA FACILE
